// Logisim project ProiectParcare.circ as structural Verilog
module main (
);

  wire Clk_out, iesire1_1_iesire_1, iesire2_1_iesire_2, intrare1_1_intrare_1, intrare2_1_intrare_2,
       Reset_out, Senzors_p1, Senzors_p2, Senzors_p3, Senzors_p4, Senzors_p5, Senzors_p6, Senzors_p7,
       Senzors_p8, ssd_1_a, ssd_1_b, ssd_1_c, ssd_1_d, ssd_1_e, ssd_1_f, ssd_1_g, ssd_2_a, ssd_2_b, ssd_2_c,
       ssd_2_d, ssd_2_e, ssd_2_f, ssd_2_g, unitate_de_control_1_empty, unitate_de_control_1_full,
       unitate_de_control_1_parking_in, unitate_de_control_1_parking_out;
  wire [7:0] unitate_de_control_1_p_counter;

  Button Reset (.out(Reset_out));
  Clock Clk (.out(Clk_out));
  // DipSwitch Senzors: pin names not known; wires that end beside it: Senzors_p1, Senzors_p2, Senzors_p3, Senzors_p4, Senzors_p5, Senzors_p6, Senzors_p7, Senzors_p8
  Unitate_de_control unitate_de_control_1 (
    .reset(Reset_out), .clock(Clk_out), .intrare_1(intrare1_1_intrare_1), .intrare_2(intrare2_1_intrare_2),
    .iesire_1(iesire1_1_iesire_1), .iesire_2(iesire2_1_iesire_2), .full(unitate_de_control_1_full),
    .empty(unitate_de_control_1_empty), .p_counter(unitate_de_control_1_p_counter),
    .parking_in(unitate_de_control_1_parking_in), .parking_out(unitate_de_control_1_parking_out));
  LED Full (.in(unitate_de_control_1_full));
  LED Parking_in (.in(unitate_de_control_1_parking_in));
  LED Parking_out (.in(unitate_de_control_1_parking_out));
  LED Empty (.in(unitate_de_control_1_empty));
  Intrare1 intrare1_1 (
    .Reset(Reset_out), .CLK(Clk_out), .s1(Senzors_p1), .s2(Senzors_p2), .intrare_1(intrare1_1_intrare_1));
  Intrare2 intrare2_1 (
    .Reset(Reset_out), .CLK(Clk_out), .s1(Senzors_p3), .s2(Senzors_p4), .intrare_2(intrare2_1_intrare_2));
  Iesire1 iesire1_1 (.Reset(Reset_out), .CLK(Clk_out), .s1(Senzors_p5), .s2(Senzors_p6), .iesire_1(iesire1_1_iesire_1));
  Iesire2 iesire2_1 (.Reset(Reset_out), .CLK(Clk_out), .s1(Senzors_p7), .s2(Senzors_p8), .iesire_2(iesire2_1_iesire_2));
  ssd ssd_1 (
    .B0(unitate_de_control_1_p_counter[7]), .B1(unitate_de_control_1_p_counter[6]),
    .B2(unitate_de_control_1_p_counter[5]), .B3(unitate_de_control_1_p_counter[4]), .A(ssd_1_a), .B(ssd_1_b),
    .C(ssd_1_c), .D(ssd_1_d), .E(ssd_1_e), .F(ssd_1_f), .G(ssd_1_g));
  ssd ssd_2 (
    .B0(unitate_de_control_1_p_counter[3]), .B1(unitate_de_control_1_p_counter[2]),
    .B2(unitate_de_control_1_p_counter[1]), .B3(unitate_de_control_1_p_counter[0]), .A(ssd_2_a), .B(ssd_2_b),
    .C(ssd_2_c), .D(ssd_2_d), .E(ssd_2_e), .F(ssd_2_f), .G(ssd_2_g));
  _7_Segment_Display u_7_segment_display_1 (
    .g(ssd_1_g), .f(ssd_1_f), .a(ssd_1_a), .b(ssd_1_b), .e(ssd_1_e), .d(ssd_1_d), .c(ssd_1_c));  // open: dp
  _7_Segment_Display u_7_segment_display_2 (
    .g(ssd_2_g), .f(ssd_2_f), .a(ssd_2_a), .b(ssd_2_b), .e(ssd_2_e), .d(ssd_2_d), .c(ssd_2_c));  // open: dp

  // Notes on the sheet:
  //   Afisor parcare
endmodule

// VHDL entity Intrare1, as the project stores it:
LIBRARY ieee;
USE ieee.std_logic_1164.all;
USE ieee.std_logic_UNSIGNED.all;
USE ieee.numeric_std.all;

ENTITY Intrare1 IS

  PORT (
		Reset: in std_logic;
        	CLK: in std_logic;
        	s1,s2: in std_logic;
        	intrare_1: out std_logic
        );
END Intrare1;

ARCHITECTURE TypeArchitecture OF Intrare1 IS
type state is (idle,st1,st2,st3,final);
signal stare,nxstare:state := idle;
signal senzor : std_logic_vector(1 downto 0);

begin

senzor(0) <= s2;
senzor(1) <= s1;
process(clk,reset)
begin
	if reset='1' then stare<=idle;
	else
	if rising_edge(clk) then
		stare<=nxstare;
	end if;
	end if;
end process;

process(clk)
  begin
  if ( rising_edge(clk) ) then
    	case stare is
      when idle =>
        if ( senzor = "00" ) then
          intrare_1 <= '0';
          nxstare <= st1;
        else
          intrare_1 <= '0';
          nxstare <= idle;
        end if;

      when st1 =>
        if ( senzor = "10" ) then
          intrare_1 <= '1';
          nxstare <= st2;
        else
          intrare_1 <= '0';
          nxstare <= st1;
        end if;

      when st2 =>
        if ( senzor = "11" ) then
          intrare_1 <= '0';
          nxstare <= st3;
        else
          intrare_1 <= '0';
          nxstare <= st2;
        end if;

      when st3 =>
        if ( senzor = "01" ) then
        	intrare_1 <= '0';
          nxstare <= final;
        else
          intrare_1 <= '0';
          nxstare <= st3;
        end if;

      when final =>
        if ( senzor = "00" ) then
          intrare_1 <= '0';
          nxstare <= idle;
        else
          intrare_1 <= '0';
          nxstare <= idle;
        end if;
      when others => intrare_1 <= '0'; nxstare <= idle;
    end case;
    end if;

  end process;


END TypeArchitecture;

// VHDL entity ssd, as the project stores it:
library ieee;
use ieee.std_logic_1164.all;

entity ssd is
Port ( B0,B1,B2,B3 : in STD_LOGIC;
A,B,C,D,E,F,G : out STD_LOGIC);
end ssd;
 
architecture Behavioral of ssd is
 
begin
 
A <= B0 OR B2 OR (B1 AND B3) OR (NOT B1 AND NOT B3);
B <= (NOT B1) OR (NOT B2 AND NOT B3) OR (B2 AND B3);
C <= B1 OR NOT B2 OR B3;
D <= (NOT B1 AND NOT B3) OR (B2 AND NOT B3) OR (B1 AND NOT B2 AND B3) OR (NOT B1 AND B2) OR B0;
E <= (NOT B1 AND NOT B3) OR (B2 AND NOT B3);
F <= B0 OR (NOT B2 AND NOT B3) OR (B1 AND NOT B2) OR (B1 AND NOT B3);
G <= B0 OR (B1 AND NOT B2) OR ( NOT B1 AND B2) OR (B2 AND NOT B3);

end architecture;

// VHDL entity Intrare2, as the project stores it:
LIBRARY ieee;
USE ieee.std_logic_1164.all;
USE ieee.std_logic_UNSIGNED.all;
USE ieee.numeric_std.all;

ENTITY Intrare2 IS

  PORT (
		Reset: in std_logic;
        	CLK: in std_logic;
        	s1,s2: in std_logic;
        	intrare_2: out std_logic
        );
END Intrare2;

ARCHITECTURE TypeArchitecture OF Intrare2 IS
type state is (idle,st1,st2,st3,final);
signal stare,nxstare:state := idle;
signal senzor : std_logic_vector(1 downto 0);

begin

senzor(0) <= s2;
senzor(1) <= s1;
process(clk,reset)
begin
	if reset='1' then stare<=idle;
	else
	if rising_edge(clk) then
		stare<=nxstare;
	end if;
	end if;
end process;

process(clk)
  begin
  if ( rising_edge(clk) ) then
    	case stare is
      when idle =>
        if ( senzor = "00" ) then
          intrare_2 <= '0';
          nxstare <= st1;
        else
          intrare_2 <= '0';
          nxstare <= idle;
        end if;

      when st1 =>
        if ( senzor = "10" ) then
          intrare_2 <= '1';
          nxstare <= st2;
        else
          intrare_2 <= '0';
          nxstare <= st1;
        end if;

      when st2 =>
        if ( senzor = "11" ) then
          intrare_2 <= '0';
          nxstare <= st3;
        else
          intrare_2 <= '0';
          nxstare <= st2;
        end if;

      when st3 =>
        if ( senzor = "01" ) then
          intrare_2 <= '0';
          nxstare <= final;
        else
          intrare_2 <= '0';
          nxstare <= st3;
        end if;

      when final =>
        if ( senzor = "00" ) then
          intrare_2 <= '0';
          nxstare <= idle;
        else
          intrare_2 <= '0';
          nxstare <= idle;
        end if;
      when others => intrare_2 <= '0'; nxstare <= idle;
    end case;
    end if;

  end process;


END TypeArchitecture;

// VHDL entity Iesire1, as the project stores it:
LIBRARY ieee;
USE ieee.std_logic_1164.all;
USE ieee.std_logic_UNSIGNED.all;
USE ieee.numeric_std.all;

ENTITY Iesire1 IS

  PORT (
		Reset: in std_logic;
        	CLK: in std_logic;
        	s1,s2: in std_logic;
        	iesire_1: out std_logic
        );
END Iesire1;

ARCHITECTURE TypeArchitecture OF Iesire1 IS
type state is (idle,st1,st2,st3,final);
signal stare,nxstare:state := idle;
signal senzor : std_logic_vector(1 downto 0);

begin

senzor(0) <= s2;
senzor(1) <= s1;
process(clk,reset)
begin
	if reset='1' then stare<=idle;
	else
	if rising_edge(clk) then
		stare<=nxstare;
	end if;
	end if;
end process;

process(clk)
  begin
  if ( rising_edge(clk) ) then
    	case stare is
      when idle =>
        if ( senzor = "00" ) then
          iesire_1 <= '0';
          nxstare <= st1;
        else
          iesire_1 <= '0';
          nxstare <= idle;
        end if;

      when st1 =>
        if ( senzor = "10" ) then
          iesire_1 <= '1';
          nxstare <= st2;
        else
          iesire_1 <= '0';
          nxstare <= st1;
        end if;

      when st2 =>
        if ( senzor = "11" ) then
          iesire_1 <= '0';
          nxstare <= st3;
        else
          iesire_1 <= '0';
          nxstare <= st2;
        end if;

      when st3 =>
        if ( senzor = "01" ) then
          iesire_1 <= '0';
          nxstare <= final;
        else
          iesire_1 <= '0';
          nxstare <= st3;
        end if;

      when final =>
        if ( senzor = "00" ) then
          iesire_1 <= '0';
          nxstare <= idle;
        else
          iesire_1 <= '0';
          nxstare <= idle;
        end if;
      when others => iesire_1 <= '0'; nxstare <= idle;
    end case;
    end if;

  end process;


END TypeArchitecture;

// VHDL entity Iesire2, as the project stores it:
LIBRARY ieee;
USE ieee.std_logic_1164.all;
USE ieee.std_logic_UNSIGNED.all;
USE ieee.numeric_std.all;

ENTITY Iesire2 IS

  PORT (
		Reset: in std_logic;
        	CLK: in std_logic;
        	s1,s2: in std_logic;
        	iesire_2: out std_logic
        );
END Iesire2;

ARCHITECTURE TypeArchitecture OF Iesire2 IS
type state is (idle,st1,st2,st3,final);
signal stare,nxstare:state := idle;
signal senzor : std_logic_vector(1 downto 0);

begin

senzor(0) <= s2;
senzor(1) <= s1;
process(clk,reset)
begin
	if reset='1' then stare<=idle;
	else
	if rising_edge(clk) then
		stare<=nxstare;
	end if;
	end if;
end process;

process(clk)
  begin
  if ( rising_edge(clk) ) then
    	case stare is
      when idle =>
        if ( senzor = "00" ) then
          iesire_2 <= '0';
          nxstare <= st1;
        else
          iesire_2 <= '0';
          nxstare <= idle;
        end if;

      when st1 =>
        if ( senzor = "10" ) then
          iesire_2 <= '1';
          nxstare <= st2;
        else
          iesire_2 <= '0';
          nxstare <= st1;
        end if;

      when st2 =>
        if ( senzor = "11" ) then
          iesire_2 <= '0';
          nxstare <= st3;
        else
          iesire_2 <= '0';
          nxstare <= st2;
        end if;

      when st3 =>
        if ( senzor = "01" ) then
          iesire_2 <= '0';
          nxstare <= final;
        else
          iesire_2 <= '0';
          nxstare <= st3;
        end if;

      when final =>
        if ( senzor = "00" ) then
          iesire_2 <= '0';
          nxstare <= idle;
        else
          iesire_2 <= '0';
          nxstare <= idle;
        end if;
      when others => iesire_2 <= '0'; nxstare <= idle;
    end case;
    end if;

  end process;


END TypeArchitecture;

// VHDL entity Unitate_de_control, as the project stores it:
LIBRARY ieee;
USE ieee.std_logic_1164.all;
USE ieee.numeric_std.all;
USE ieee.std_logic_unsigned.all;

ENTITY Unitate_de_control IS
  PORT (
    reset       : in  std_logic;
    clock       : in  std_logic;
    intrare_1   : in  std_logic;
    intrare_2   : in  std_logic;
    iesire_1    : in  std_logic;
    iesire_2    : in  std_logic;
    full        : out std_logic;
    empty       : out std_logic;
    p_counter   : out std_logic_vector(7 downto 0);
    parking_in : out std_logic; 
    parking_out : out std_logic  
  );
END Unitate_de_control;

ARCHITECTURE TypeArchitecture OF Unitate_de_control IS

  SIGNAL counter : std_logic_vector(7 downto 0) := "00110000"; 

BEGIN

process(intrare_1, intrare_2, iesire_1, iesire_2, reset)
  begin
  	if ( reset = '1' ) then 
  		counter <= "00110000";
  	else
  		if ( intrare_1 = '1' or intrare_2 = '1' ) then
  			if (  counter > "00000000"  ) then
				if ( counter( 3 downto 0 ) = "0000" ) then
					counter( 3 downto 0 ) <= "1001";
					counter( 7 downto 4 ) <= counter( 7 downto 4 ) - 1;
				else
					counter <= counter - 1;
				end if;
			end if;
  		end if;
  		 if ( iesire_1 = '1' or iesire_2 = '1' ) then
  			if (  counter < "00110000"  ) then
				if ( counter( 3 downto 0 ) = "1001" ) then
					counter( 3 downto 0 ) <= "0000";
					counter( 7 downto 4 ) <= counter( 7 downto 4 ) + 1;
				else
					counter <= counter + 1;
				end if;
  			end if;
		end if;

	    p_counter <= counter;
	    
	    if counter = "00000000" then  
	      full <= '1';
	      empty <= '0';
	    elsif counter = "00110000" then 
	      full <= '0';
	      empty <= '1';
	    else
	      full <= '0';
	      empty <= '0';
	    end if;
	
	    
	    if ( intrare_1 = '1' or intrare_2 = '1' ) then
	      parking_in <= '1'; 
	    else
	      parking_in <= '0'; 
	    end if;
	
	    if ( iesire_1 = '1' or iesire_2 = '1' ) then
	      parking_out <= '1'; 
	    else
	      parking_out <= '0'; 
	    end if;
    end if;
end process;

END TypeArchitecture;
